# Fritzing sketch Fritzing Diagram (saved by Fritzing 0.9.3b)
breadboards: 1

parts:
  Part1 = Arduino Uno (Rev3)
  Part2 = Motor Driver 1A Dual TB6612FNG  # not connected
  S1 = Toggle Switch [package=THT]
  M1 = DC Motor  # not connected
  M2 = DC Motor  # not connected

nets:
  N1: Part1.D7, S1.L1
  N2: Part1.GND, S1.COM
