# Fritzing sketch Fritz Diagram For LED (saved by Fritzing 0.9.3b)
breadboards: 1

parts:
  Part1 = Arduino Uno (Rev3)
  LED1 = LED - 5mm [color="Red (633nm)" package="5 mm [THT]"]
  LED2 = LED - 5mm [color="Blue (470nm)" package="5 mm [THT]"]
  LED3 = LED - 5mm [color="Green (555nm)" package="5 mm [THT]"]
  R1 = Resistor [tolerance=±5% resistance=220 package=THT]
  R2 = Resistor [tolerance=±5% resistance=220 package=THT]
  R3 = Resistor [tolerance=±5% resistance=220 package=THT]
  J1 = Piezo Speaker

nets:
  N1: Part1.D10_PWM/SS, J1.pin1
  N2: Part1.D11_PWM/MOSI, R1.Pin_0
  N3: Part1.D12/MISO, R2.Pin_0
  N4: Part1.D13/SCK, R3.Pin_0
  N5: Part1.GND, LED1.anode, LED2.anode, LED3.anode, J1.pin2
  N6: LED1.cathode, R3.Pin_1
  N7: LED2.cathode, R2.Pin_1
  N8: LED3.cathode, R1.Pin_1
