# Fritzing sketch FritzingDiagram (saved by Fritzing 0.9.3b)
breadboards: 1

parts:
  Part1 = Arduino Uno (Rev3)
  LED1 = LED - 5mm [color="Red (633nm)" package="5 mm [THT]"]
  R1 = Resistor [tolerance=±5% resistance=220 package=THT]
  Part2 = Breakout Board for Electret Microphone
  R2 = Resistor [tolerance=±5% resistance=220 package=THT]
  R3 = Resistor [tolerance=±5% resistance=220 package=THT]
  LED2 = LED - 5mm [color="Blue (470nm)" package="5 mm [THT]"]
  LED3 = LED - 5mm [color="Green (560nm)" package="5 mm [THT]"]
  LED4 = LED - 5mm [color="Yellow (574nm)" package="5 mm [THT]"]
  R4 = Resistor [tolerance=±5% resistance=220 package=THT]

nets (from the schematic view):
  N1: Part1.A0, Part2.AUD
  N2: Part1.D9_PWM, Part2.GND
  N3: Part1.D10_PWM/SS, R4.Pin_1
  N4: Part1.D11_PWM/MOSI, R3.Pin_1
  N5: Part1.D12/MISO, R2.Pin_1
  N6: Part1.D13/SCK, R1.Pin_1
  N7: Part1.GND, LED2.anode, LED3.anode
  N8: LED1.anode, R1.Pin_0
  N9: R2.Pin_0, LED2.cathode
  N10: R3.Pin_0, LED3.cathode
  N11: LED4.cathode, R4.Pin_0

// code stored in the sketch: EnvironmentSoundTracker.ino
#define MPHONE A0//defines which analog to feed through

int sense = 0;//sets up variable to adjust the sensitivity of the microphone
void setup() {
  pinMode(MPHONE, INPUT);
  pinMode (13, OUTPUT);
  pinMode (12, OUTPUT);
  pinMode (11, OUTPUT);
  pinMode (10, OUTPUT);
  Serial.begin(9600);

}

void loop() {
  sense = analogRead(MPHONE) * 50; //used to increase the microphone's sensitivity as well as variable range

//Red
//Lights up during timid levels of sound
 if (sense > 1 && sense < 450){
  digitalWrite(13, HIGH);
  delay(200);
  }
  else {
    digitalWrite(13, LOW);
    delay(200);
    }
    
//Green
//Usually should light up during average sound levels
 if (sense > 450 && sense < 700){
  digitalWrite(12, HIGH);
  delay(200);
  } 
  else {
    digitalWrite(12, LOW);
    delay(200);
    }
    
//Blue
//Will light up during above average sound levels (i.e: crowded building, construction, etc)    
 if (sense > 700 && sense < 950){
  digitalWrite(11, HIGH);
  delay(200);
  } 
  else {
    digitalWrite(11, LOW);
    delay(200);
    }
    
//Yellow
//Will only light up if sound levels are extreme.
 if (sense > 950){
  digitalWrite(10, HIGH);
  delay(200);
  } 
  else {
    digitalWrite(10, LOW);
    delay(200);
    }
  Serial.println(analogRead(MPHONE) * 50, DEC);
  delay(200);
}
